# Fritzing sketch Esquema_montaje_caro (saved by Fritzing 0.9.3b)
breadboards: 1

parts:
  WeMos_D1_R1 = WeMos D1 R2
  Componente1 = FC-28 Soil Hygrometer Module
  Componente2 = Soil Moisture Sensor
  YL-83_-_Detection_Board1 = YL-83 Rain Sensor - Detection Board
  LED1 = LEDs [package=led10mm]
  Componente3 = FC-28 Soil Hygrometer Module
  Componente5 = Adafruit TSL2591 [part_number="Adafruit #1980"]

nets:
  N1: WeMos_D1_R1.D3, LED1.A
  N2: WeMos_D1_R1.(D6), Componente3.DO
  N3: WeMos_D1_R1.D14, Componente5.SDA
  N4: WeMos_D1_R1.D15, Componente5.SCL
  N5: WeMos_D1_R1.A0, Componente1.AO
  GND: WeMos_D1_R1.GND, Componente1.GND, LED1.C, Componente3.GND, Componente5.GND
  VCC: WeMos_D1_R1.5V, Componente1.VCC, Componente3.VCC, Componente5.VIN
  N6: Componente1.POS, Componente2.VCC
  N7: Componente1.NEG, Componente2.GND
  N8: YL-83_-_Detection_Board1.POS, Componente3.POS
  N9: YL-83_-_Detection_Board1.NEG, Componente3.NEG

custom parts:
  WeMos D1 R2: The D1 R2 is a mini wifi board based on the ESP-8266EX.
  FC-28 Soil Hygrometer Module: The FC-28 is a soil hygrometer module that uses the Texas Instruments LM393 comparator chip to provide an analog measurement of soil humidity. The digital output is high when soil moisture is over a certain threshold, as determined by adjusting the potentiometer.
  YL-83 Rain Sensor - Detection Board: The YL-83 is a rain sensor that has more resistance when dry and less resistance when wet. The module runs at 5V.
  Adafruit TSL2591: When the future is dazzlingly-bright, this ultra-high-range luminosity sensor will help you measure it. The TSL2591 luminosity sensor is an advanced digital light sensor, ideal for use in a wide range of light situations. Compared to low cost CdS cells, this sensor is more precise, allowing for exact lux calculations and can be configured for different gain/timing ranges to detect light ranges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
