# Fritzing sketch Esquema de montaje (saved by Fritzing 0.9.3b)
breadboards: 1

parts:
  WeMos_D1_R1 = WeMos D1 R2
  Componente1 = FC-28 Soil Hygrometer Module
  Componente2 = Soil Moisture Sensor
  YL-83_-_Detection_Board1 = YL-83 Rain Sensor - Detection Board
  DHT1 = DHT11 Humitidy and Temperature Sensor
  LED1 = LEDs [package=led10mm]
  Componente3 = FC-28 Soil Hygrometer Module
  R1 = Photocell (LDR) [package=THT]
  R2 = Resistor [tolerance=±5% resistance=1k package="2010 [SMD]"]

nets (from the breadboard view):
  N1: WeMos_D1_R1.D3, LED1.A
  N2: WeMos_D1_R1.(D5), DHT1.DATA, R2.Pin_0
  N3: WeMos_D1_R1.(D6), Componente3.DO
  N4: WeMos_D1_R1.(D7), R1.pin_1
  N5: WeMos_D1_R1.A0, Componente1.AO
  GND: WeMos_D1_R1.GND#21, Componente1.GND, DHT1.GND, LED1.C, Componente3.GND
  VCC: WeMos_D1_R1.5V, Componente1.VCC, DHT1.VDD, Componente3.VCC, R1.pin_0, R2.Pin_1
  N6: Componente1.POS, Componente2.VCC
  N7: Componente1.NEG, Componente2.GND
  N8: YL-83_-_Detection_Board1.POS, Componente3.POS
  N9: YL-83_-_Detection_Board1.NEG, Componente3.NEG

custom parts:
  WeMos D1 R2: The D1 R2 is a mini wifi board based on the ESP-8266EX.
  FC-28 Soil Hygrometer Module: The FC-28 is a soil hygrometer module that uses the Texas Instruments LM393 comparator chip to provide an analog measurement of soil humidity. The digital output is high when soil moisture is over a certain threshold, as determined by adjusting the potentiometer.
  YL-83 Rain Sensor - Detection Board: The YL-83 is a rain sensor that has more resistance when dry and less resistance when wet. The module runs at 5V.
  DHT11 Humitidy and Temperature Sensor: DHT11 Humidity and Temperature Sensor
